# Fritzing sketch CarControlled(FritzingFile) (saved by Fritzing 0.9.0b)
breadboards: 1

parts:
  Part1 = Arduino Uno (Rev3)
  IC2 = IC, DIP package, 16 pins [chip_label=L293D spacing=300mil]
  Part2 = Bluetooth HC-05 Macho
  M1 = DC Motor
  M2 = DC Motor
  LED1 = LEDs [package=led10mm]
  VCC2 = Battery block 9V

nets:
  N1: Part1.D8, IC2.pin15
  N2: Part1.D9_PWM, IC2.pin10
  N3: Part1.D10_PWM/SS, IC2.pin2
  N4: Part1.D11_PWM/MOSI, IC2.pin7
  N5: Part1.D0/RX, Part2.TXD
  N6: Part1.D1/TX, Part2.RXD
  N7: Part1.D7, LED1.C
  5V: Part1.5V, IC2.pin16, Part2.VCC
  GND: Part1.GND, Part2.GND, LED1.A
  N8: IC2.pin3, M2.pin_2
  N9: IC2.pin4, IC2.pin5, IC2.pin12, IC2.pin13, VCC2.-
  N10: IC2.pin6, M1.pin_1
  N11: IC2.pin8, VCC2.+
  N12: IC2.pin11, M2.pin_1
  N13: IC2.pin14, M1.pin_2

notes:
  <-------Left Motor
  Right Motor---->
